// Logisim project Contador.circ as structural Verilog: 5 circuits, main circuit main
module main (
  input  in_1,
  input  in_2,
  input  in_3,
  input  in_4,
  input  in_5,
  output out_6,
  output out_7,
  output out_8
);

  not not_1 (out_8, in_5);
  or or_1 (out_6, in_1, in_2);
  and and_1 (out_7, in_3, in_4);
endmodule

module Ejemplo_Sebastian (
  input  A,
  input  B,
  input  A_2,
  input  B_2,
  output out_5,
  output Y
);

  wire and_1_out, and_2_out, not_1_out, not_2_out;

  not not_1 (not_1_out, A_2);
  not not_2 (not_2_out, B_2);
  xor xor_1 (out_5, A, B);
  and and_1 (and_1_out, not_1_out, B_2);
  and and_2 (and_2_out, A_2, not_2_out);
  or or_1 (Y, and_1_out, and_2_out);
endmodule

module Display_de_7_segmentos (
  input  A3,
  input  A2,
  input  A1,
  input  A0,
  output a,
  output b,
  output c,
  output d,
  output e,
  output f,
  output g
);

  wire and_1_out, and_2_out, and_3_out, and_4_out, and_5_out, and_6_out, and_7_out, and_8_out, and_9_out,
       and_10_out, and_11_out, and_12_out, and_13_out, and_14_out, and_15_out, and_16_out, not_1_out,
       not_2_out, not_3_out, not_4_out, not_5_out, not_6_out, not_7_out, not_8_out, not_9_out, not_10_out,
       not_11_out, not_12_out, not_13_out, not_14_out, not_15_out, not_16_out, not_17_out, not_18_out,
       not_19_out, not_20_out, not_21_out;

  not not_1 (not_1_out, A2);
  and and_1 (and_1_out, not_1_out, not_2_out);
  not not_2 (not_2_out, A0);
  and and_2 (and_2_out, A2, A0);
  not not_3 (not_3_out, A2);
  not not_4 (not_4_out, A1);
  and and_3 (and_3_out, not_4_out, not_5_out);
  not not_5 (not_5_out, A0);
  and and_4 (and_4_out, A1, A0);
  not not_6 (not_6_out, A1);
  or or_1 (c, not_6_out, A0, A2);
  not not_7 (not_7_out, A2);
  and and_5 (and_5_out, not_7_out, not_8_out);
  not not_8 (not_8_out, A0);
  not not_9 (not_9_out, A2);
  and and_6 (and_6_out, not_9_out, A1);
  and and_7 (and_7_out, A1, not_10_out);
  not not_10 (not_10_out, A0);
  and and_8 (and_8_out, A2, not_11_out, A0);
  not not_11 (not_11_out, A1);
  not not_12 (not_12_out, A2);
  and and_9 (and_9_out, not_12_out, not_13_out);
  not not_13 (not_13_out, A0);
  and and_10 (and_10_out, A1, not_14_out);
  not not_14 (not_14_out, A0);
  not not_15 (not_15_out, A1);
  and and_11 (and_11_out, not_15_out, not_16_out);
  not not_16 (not_16_out, A0);
  and and_12 (and_12_out, A2, not_17_out);
  not not_17 (not_17_out, A1);
  and and_13 (and_13_out, A2, not_18_out);
  not not_18 (not_18_out, A0);
  not not_19 (not_19_out, A2);
  and and_14 (and_14_out, not_19_out, A1);
  and and_15 (and_15_out, A2, not_20_out);
  not not_20 (not_20_out, A1);
  and and_16 (and_16_out, A2, not_21_out);
  not not_21 (not_21_out, A0);
  or or_2 (a, and_1_out, A1, and_2_out, A3);
  or or_3 (b, not_3_out, and_3_out, and_4_out);
  or or_4 (d, and_5_out, and_6_out, and_7_out, and_8_out);
  or or_5 (e, and_9_out, and_10_out);
  or or_6 (f, and_11_out, and_12_out, and_13_out, A3);
  or or_7 (g, and_14_out, and_15_out, and_16_out, A3);
  _7_Segment_Display u_7_segment_display_1 (.g(g), .f(f), .a(a), .b(b), .e(e), .d(d), .c(c));  // open: dp
endmodule

module Biestables (
  input  in_1,
  output out_2
);

  wire clock_1_out;

  Clock clock_1 (.out(clock_1_out));
  D_Flip_Flop d_ff_1 (.clk(clock_1_out), .D(in_1), .Q(out_2));  // open: Qn, preset, en, reset
endmodule

module Contador (
  output a,
  output b,
  output c,
  output d,
  output e,
  output f,
  output g
);

  wire and_1_out, and_2_out, and_3_out, and_4_out, and_5_out, and_6_out, and_7_out, and_8_out, and_9_out,
       and_10_out, and_11_out, and_12_out, and_13_out, and_14_out, and_15_out, and_16_out, and_17_out,
       and_18_out, and_19_out, and_20_out, and_21_out, and_22_out, and_23_out, clock_1_out, d_ff_1_q,
       d_ff_2_q, d_ff_3_q, d_ff_4_q, not_1_out, not_2_out, not_3_out, not_4_out, not_5_out, not_6_out,
       not_7_out, not_8_out, not_9_out, not_10_out, not_11_out, not_12_out, not_13_out, not_14_out,
       not_15_out, not_16_out, not_17_out, not_18_out, not_19_out, not_20_out, not_21_out, not_22_out,
       not_23_out, not_24_out, not_25_out, not_26_out, not_27_out, not_28_out, not_29_out, or_1_out,
       or_2_out, or_3_out;

  and and_1 (and_1_out, d_ff_2_q, d_ff_3_q, d_ff_4_q);
  and and_2 (and_2_out, d_ff_1_q, not_1_out);
  not not_1 (not_1_out, d_ff_4_q);
  not not_2 (not_2_out, d_ff_2_q);
  and and_3 (and_3_out, not_2_out, d_ff_3_q, d_ff_4_q);
  and and_4 (and_4_out, d_ff_2_q, not_3_out);
  not not_3 (not_3_out, d_ff_3_q);
  and and_5 (and_5_out, d_ff_2_q, not_4_out);
  not not_4 (not_4_out, d_ff_4_q);
  not not_5 (not_5_out, d_ff_1_q);
  and and_6 (and_6_out, not_5_out, not_6_out, d_ff_4_q);
  not not_6 (not_6_out, d_ff_3_q);
  and and_7 (and_7_out, d_ff_3_q, not_7_out);
  not not_7 (not_7_out, d_ff_4_q);
  not not_8 (not_8_out, d_ff_4_q);
  or or_1 (or_1_out, and_1_out, and_2_out);
  or or_2 (or_2_out, and_3_out, and_4_out, and_5_out);
  or or_3 (or_3_out, and_6_out, and_7_out);
  Clock clock_1 (.out(clock_1_out));
  D_Flip_Flop d_ff_1 (.clk(clock_1_out), .D(or_1_out), .Q(d_ff_1_q));  // open: Qn, preset, en, reset
  D_Flip_Flop d_ff_2 (.clk(clock_1_out), .D(or_2_out), .Q(d_ff_2_q));  // open: Qn, preset, en, reset
  D_Flip_Flop d_ff_3 (.clk(clock_1_out), .D(or_3_out), .Q(d_ff_3_q));  // open: Qn, preset, en, reset
  D_Flip_Flop d_ff_4 (.clk(clock_1_out), .D(not_8_out), .Q(d_ff_4_q));  // open: Qn, preset, en, reset
  not not_9 (not_9_out, d_ff_2_q);
  not not_10 (not_10_out, d_ff_4_q);
  not not_11 (not_11_out, d_ff_3_q);
  not not_12 (not_12_out, d_ff_4_q);
  not not_13 (not_13_out, d_ff_3_q);
  not not_14 (not_14_out, d_ff_2_q);
  not not_15 (not_15_out, d_ff_4_q);
  not not_16 (not_16_out, d_ff_2_q);
  not not_17 (not_17_out, d_ff_4_q);
  not not_18 (not_18_out, d_ff_3_q);
  not not_19 (not_19_out, d_ff_2_q);
  not not_20 (not_20_out, d_ff_4_q);
  not not_21 (not_21_out, d_ff_4_q);
  not not_22 (not_22_out, d_ff_3_q);
  not not_23 (not_23_out, d_ff_4_q);
  not not_24 (not_24_out, d_ff_3_q);
  not not_25 (not_25_out, d_ff_4_q);
  not not_26 (not_26_out, d_ff_2_q);
  not not_27 (not_27_out, d_ff_3_q);
  not not_28 (not_28_out, d_ff_4_q);
  and and_8 (and_8_out, not_9_out, not_10_out);
  and and_9 (and_9_out, d_ff_2_q, d_ff_4_q);
  not not_29 (not_29_out, d_ff_2_q);
  and and_10 (and_10_out, not_11_out, not_12_out);
  and and_11 (and_11_out, d_ff_3_q, d_ff_4_q);
  or or_4 (c, not_13_out, d_ff_4_q, d_ff_2_q);
  and and_12 (and_12_out, not_14_out, not_15_out);
  and and_13 (and_13_out, not_16_out, d_ff_3_q);
  and and_14 (and_14_out, d_ff_3_q, not_17_out);
  and and_15 (and_15_out, d_ff_2_q, not_18_out, d_ff_4_q);
  and and_16 (and_16_out, not_19_out, not_20_out);
  and and_17 (and_17_out, d_ff_3_q, not_21_out);
  and and_18 (and_18_out, not_22_out, not_23_out);
  and and_19 (and_19_out, d_ff_2_q, not_24_out);
  and and_20 (and_20_out, d_ff_2_q, not_25_out);
  and and_21 (and_21_out, not_26_out, d_ff_3_q);
  and and_22 (and_22_out, d_ff_2_q, not_27_out);
  and and_23 (and_23_out, d_ff_2_q, not_28_out);
  or or_5 (a, and_8_out, d_ff_3_q, and_9_out, d_ff_1_q);
  or or_6 (b, not_29_out, and_10_out, and_11_out);
  or or_7 (d, and_12_out, and_13_out, and_14_out, and_15_out);
  or or_8 (e, and_16_out, and_17_out);
  or or_9 (f, and_18_out, and_19_out, and_20_out, d_ff_1_q);
  or or_10 (g, and_21_out, and_22_out, and_23_out, d_ff_1_q);
  _7_Segment_Display u_7_segment_display_1 (.g(g), .f(f), .a(a), .b(b), .e(e), .d(d), .c(c));  // open: dp
endmodule
