// Logisim project Parcial2.circ as structural Verilog: 11 circuits, main circuit main
module main (
  input  [7:0] _0000,
  input  [7:0] _0001,
  input  [7:0] _0010,
  input  [15:0] A,
  input  [7:0] _0011,
  input  [15:0] _0,
  input  _1_Para_Complemento_2,
  input  [7:0] _0100,
  input  [15:0] B,
  input  [7:0] _0101,
  input  [7:0] _0110,
  input  _1_Para_Complemento_2_2,
  input  [7:0] _0111,
  input  [7:0] _1000,
  input  [7:0] _1001,
  input  [7:0] _1010,
  input  [7:0] _1011,
  input  [7:0] _1100,
  input  [7:0] _1101,
  input  [7:0] _1110,
  input  [7:0] _1111,
  input  [3:0] in_22,
  input  [3:0] in_23,
  output [7:0] _0000_2,
  output [7:0] _0001_2,
  output [7:0] _0010_2,
  output [7:0] _0011_2,
  output [7:0] _0100_2,
  output [7:0] _0101_2,
  output [7:0] _0110_2,
  output [7:0] _0111_2,
  output [7:0] _1000_2,
  output [7:0] _1001_2,
  output [7:0] _1010_2,
  output [7:0] _1011_2,
  output [7:0] _1100_2,
  output [7:0] _1101_2,
  output [7:0] _1110_2,
  output [7:0] _1111_2,
  output out_40,
  output [15:0] C
);

  wire _1_Resta_0_Sumar_salida, A___0_out_3, A___0_out_5, A___B_out_3, and_33_out, and_34_out, B___0_out_3,
       comp_b1_1_out_4, comp_b1_2_out_4, comp_b1_3_out_4, display_1__1, display_1__2, display_1__3,
       display_1__4, display_1__5, display_1__6, display_1__7, display_1__11, display_1__22, display_1__33,
       display_1__44, display_1__55, display_1__66, display_1__77, display_1__111, display_1__222,
       display_1__333, display_1__444, display_1__555, display_1__666, display_1__777, display_1__1111,
       display_1__2222, display_1__3333, display_1__4444, display_1__5555, display_1__6666, display_1__7777,
       not_9_out, not_10_out, sumador_completo_1_acarreo, sumador_completo_2_acarreo,
       sumador_completo_3_acarreo, sumador_completo_4_acarreo, sumador_completo_5_acarreo,
       sumador_completo_6_acarreo, sumador_completo_7_acarreo, sumador_completo_8_acarreo,
       sumador_completo_9_acarreo, sumador_completo_10_acarreo, sumador_completo_11_acarreo,
       sumador_completo_12_acarreo, sumador_completo_13_acarreo, sumador_completo_14_acarreo,
       sumador_completo_15_acarreo, xor_1_out, xor_2_out, xor_3_out, xor_4_out, xor_5_out, xor_6_out,
       xor_7_out, xor_8_out, xor_9_out, xor_10_out, xor_11_out, xor_12_out, xor_13_out, xor_14_out,
       xor_15_out, xor_16_out, xor_17_out, xor_18_out;
  wire [7:0] and_1_out, and_2_out, and_3_out, and_4_out, and_5_out, and_6_out, and_7_out, and_8_out,
       and_9_out, and_10_out, and_11_out, and_12_out, and_13_out, and_14_out, and_15_out, and_16_out,
       bit_extender_1_out, bit_extender_2_out, bit_extender_3_out, bit_extender_4_out, bit_extender_5_out,
       bit_extender_6_out, bit_extender_7_out, bit_extender_8_out, not_1_out, not_2_out, not_3_out,
       not_4_out, not_5_out, not_6_out, not_7_out, not_8_out, or_1_out;
  wire [15:0] A_salida, B_salida, C_A_salida, compl_b16_1_out_2, compl_b16_2_out_2, multi_b16_1_salida,
       multi_b16_2_salida, sumador_completo_1_suma;

  assign not_1_out = ~bit_extender_1_out;  // NOT_Gate not_1, 8 bits wide
  assign bit_extender_1_out = {{7{in_22[3]}}, in_22[3]};  // Bit_Extender bit_extender_1
  assign not_2_out = ~bit_extender_2_out;  // NOT_Gate not_2, 8 bits wide
  assign bit_extender_2_out = {{7{in_22[2]}}, in_22[2]};  // Bit_Extender bit_extender_2
  assign not_3_out = ~bit_extender_3_out;  // NOT_Gate not_3, 8 bits wide
  assign bit_extender_3_out = {{7{in_22[1]}}, in_22[1]};  // Bit_Extender bit_extender_3
  assign not_4_out = ~bit_extender_4_out;  // NOT_Gate not_4, 8 bits wide
  assign bit_extender_4_out = {{7{in_22[0]}}, in_22[0]};  // Bit_Extender bit_extender_4
  assign and_1_out = _0000 & not_1_out & not_2_out & not_3_out & not_4_out;  // AND_Gate and_1, 8 bits wide
  assign and_2_out = _0001 & not_1_out & not_2_out & not_3_out & bit_extender_4_out;  // AND_Gate and_2, 8 bits wide
  assign and_3_out = _0010 & not_1_out & not_2_out & bit_extender_3_out & not_4_out;  // AND_Gate and_3, 8 bits wide
  assign and_4_out = _0011 & not_1_out & not_2_out & bit_extender_3_out & bit_extender_4_out;  // AND_Gate and_4, 8 bits wide
  assign and_5_out = _0100 & not_1_out & bit_extender_2_out & not_3_out & not_4_out;  // AND_Gate and_5, 8 bits wide
  assign and_6_out = _0101 & not_1_out & bit_extender_2_out & not_3_out & bit_extender_4_out;  // AND_Gate and_6, 8 bits wide
  assign and_7_out = _0110 & not_1_out & bit_extender_2_out & bit_extender_3_out & not_4_out;  // AND_Gate and_7, 8 bits wide
  assign and_8_out = _0111 & not_1_out & bit_extender_2_out & bit_extender_3_out & bit_extender_4_out;  // AND_Gate and_8, 8 bits wide
  assign and_9_out = _1000 & bit_extender_1_out & not_2_out & not_3_out & not_4_out;  // AND_Gate and_9, 8 bits wide
  assign and_10_out = _1001 & bit_extender_1_out & not_2_out & not_3_out & bit_extender_4_out;  // AND_Gate and_10, 8 bits wide
  assign and_11_out = _1010 & bit_extender_1_out & not_2_out & bit_extender_3_out & not_4_out;  // AND_Gate and_11, 8 bits wide
  assign and_12_out = _1011 & bit_extender_1_out & not_2_out & bit_extender_3_out & bit_extender_4_out;  // AND_Gate and_12, 8 bits wide
  assign and_13_out = _1100 & bit_extender_1_out & bit_extender_2_out & not_3_out & not_4_out;  // AND_Gate and_13, 8 bits wide
  assign and_14_out = _1101 & bit_extender_1_out & bit_extender_2_out & not_3_out & bit_extender_4_out;  // AND_Gate and_14, 8 bits wide
  assign and_15_out = _1110 & bit_extender_1_out & bit_extender_2_out & bit_extender_3_out & not_4_out;  // AND_Gate and_15, 8 bits wide
  assign and_16_out = _1111 & bit_extender_1_out & bit_extender_2_out & bit_extender_3_out & bit_extender_4_out;  // AND_Gate and_16, 8 bits wide
  assign or_1_out = and_1_out | and_2_out | and_3_out | and_4_out | and_5_out | and_6_out | and_7_out | and_8_out | and_9_out | and_10_out | and_11_out | and_12_out | and_13_out | and_14_out | and_15_out | and_16_out;  // OR_Gate or_1, 8 bits wide
  assign not_5_out = ~bit_extender_5_out;  // NOT_Gate not_5, 8 bits wide
  assign bit_extender_5_out = {{7{in_23[3]}}, in_23[3]};  // Bit_Extender bit_extender_5
  assign not_6_out = ~bit_extender_6_out;  // NOT_Gate not_6, 8 bits wide
  assign bit_extender_6_out = {{7{in_23[2]}}, in_23[2]};  // Bit_Extender bit_extender_6
  assign not_7_out = ~bit_extender_7_out;  // NOT_Gate not_7, 8 bits wide
  assign bit_extender_7_out = {{7{in_23[1]}}, in_23[1]};  // Bit_Extender bit_extender_7
  assign not_8_out = ~bit_extender_8_out;  // NOT_Gate not_8, 8 bits wide
  assign bit_extender_8_out = {{7{in_23[0]}}, in_23[0]};  // Bit_Extender bit_extender_8
  assign _0000_2 = or_1_out & not_5_out & not_6_out & not_7_out & not_8_out;  // AND_Gate and_17, 8 bits wide
  assign _0001_2 = or_1_out & not_5_out & not_6_out & not_7_out & bit_extender_8_out;  // AND_Gate and_18, 8 bits wide
  assign _0010_2 = or_1_out & not_5_out & not_6_out & bit_extender_7_out & not_8_out;  // AND_Gate and_19, 8 bits wide
  assign _0011_2 = or_1_out & not_5_out & not_6_out & bit_extender_7_out & bit_extender_8_out;  // AND_Gate and_20, 8 bits wide
  assign _0100_2 = or_1_out & not_5_out & bit_extender_6_out & not_7_out & not_8_out;  // AND_Gate and_21, 8 bits wide
  assign _0101_2 = or_1_out & not_5_out & bit_extender_6_out & not_7_out & bit_extender_8_out;  // AND_Gate and_22, 8 bits wide
  assign _0110_2 = or_1_out & not_5_out & bit_extender_6_out & bit_extender_7_out & not_8_out;  // AND_Gate and_23, 8 bits wide
  assign _0111_2 = or_1_out & not_5_out & bit_extender_6_out & bit_extender_7_out & bit_extender_8_out;  // AND_Gate and_24, 8 bits wide
  assign _1000_2 = or_1_out & bit_extender_5_out & not_6_out & not_7_out & not_8_out;  // AND_Gate and_25, 8 bits wide
  assign _1001_2 = or_1_out & bit_extender_5_out & not_6_out & not_7_out & bit_extender_8_out;  // AND_Gate and_26, 8 bits wide
  assign _1010_2 = or_1_out & bit_extender_5_out & not_6_out & bit_extender_7_out & not_8_out;  // AND_Gate and_27, 8 bits wide
  assign _1011_2 = or_1_out & bit_extender_5_out & not_6_out & bit_extender_7_out & bit_extender_8_out;  // AND_Gate and_28, 8 bits wide
  assign _1100_2 = or_1_out & bit_extender_5_out & bit_extender_6_out & not_7_out & not_8_out;  // AND_Gate and_29, 8 bits wide
  assign _1101_2 = or_1_out & bit_extender_5_out & bit_extender_6_out & not_7_out & bit_extender_8_out;  // AND_Gate and_30, 8 bits wide
  assign _1110_2 = or_1_out & bit_extender_5_out & bit_extender_6_out & bit_extender_7_out & not_8_out;  // AND_Gate and_31, 8 bits wide
  assign _1111_2 = or_1_out & bit_extender_5_out & bit_extender_6_out & bit_extender_7_out & bit_extender_8_out;  // AND_Gate and_32, 8 bits wide
  COMPL_B16 compl_b16_1 (.in_1(A), .out_2(compl_b16_1_out_2));  // open: out_3
  COMPL_B16 compl_b16_2 (.in_1(B), .out_2(compl_b16_2_out_2));  // open: out_3
  MULTI_B16 multi_b16_1 (
    .E0(A), .E1(compl_b16_1_out_2), .SELECTOR(_1_Para_Complemento_2), .ENABLE(1'b1),
    .SALIDA(multi_b16_1_salida));
  MULTI_B16 multi_b16_2 (
    .E0(B), .E1(compl_b16_2_out_2), .SELECTOR(_1_Para_Complemento_2_2), .ENABLE(1'b1),
    .SALIDA(multi_b16_2_salida));
  COMP_B16 A___0 (.A(multi_b16_1_salida), .B(_0), .out_3(A___0_out_3), .out_5(A___0_out_5));  // open: out_4
  COMP_B16 B___0 (.A(multi_b16_2_salida), .B(_0), .out_3(B___0_out_3));  // open: out_4, out_5
  COMP_B16 A___B (.A(multi_b16_1_salida), .B(multi_b16_2_salida), .out_3(A___B_out_3));  // open: out_4, out_5
  COMP_B1 comp_b1_1 (.in_1(A___0_out_3), .in_2(B___0_out_3), .out_4(comp_b1_1_out_4));  // open: out_3, out_5
  not not_9 (not_9_out, B___0_out_3);
  and and_33 (and_33_out, B___0_out_3, A___B_out_3);
  COMP_B1 comp_b1_2 (.in_1(A___0_out_5), .in_2(not_9_out), .out_4(comp_b1_2_out_4));  // open: out_3, out_5
  and and_34 (and_34_out, B___0_out_3, A___0_out_5);
  MULTI_B1 _1_Resta_0_Sumar (
    .E0(1'b1), .E1(1'b0), .SELECTOR(xor_2_out), .ENABLE(xor_1_out), .SALIDA(_1_Resta_0_Sumar_salida));
  COMP_B1 comp_b1_3 (.in_1(comp_b1_1_out_4), .in_2(A___B_out_3), .out_4(comp_b1_3_out_4));  // open: out_3, out_5
  xor xor_1 (xor_1_out, and_33_out, and_34_out);
  xor xor_2 (xor_2_out, comp_b1_3_out_4, comp_b1_2_out_4);
  not not_10 (not_10_out, xor_1_out);
  MULTI_B16 C_A (.E1(multi_b16_1_salida), .SELECTOR(not_10_out), .ENABLE(not_10_out), .SALIDA(C_A_salida));  // open: E0
  MULTI_B16 u_B (.E1(multi_b16_2_salida), .SELECTOR(xor_1_out), .ENABLE(xor_1_out), .SALIDA(B_salida));  // open: E0
  MULTI_B16 u_A (.E1(multi_b16_1_salida), .SELECTOR(xor_1_out), .ENABLE(xor_1_out), .SALIDA(A_salida));  // open: E0
  xor xor_3 (xor_3_out, B_salida[0], _1_Resta_0_Sumar_salida);
  xor xor_4 (xor_4_out, B_salida[1], _1_Resta_0_Sumar_salida);
  xor xor_5 (xor_5_out, B_salida[2], _1_Resta_0_Sumar_salida);
  xor xor_6 (xor_6_out, B_salida[3], _1_Resta_0_Sumar_salida);
  xor xor_7 (xor_7_out, B_salida[4], _1_Resta_0_Sumar_salida);
  xor xor_8 (xor_8_out, B_salida[5], _1_Resta_0_Sumar_salida);
  xor xor_9 (xor_9_out, B_salida[6], _1_Resta_0_Sumar_salida);
  xor xor_10 (xor_10_out, B_salida[7], _1_Resta_0_Sumar_salida);
  xor xor_11 (xor_11_out, B_salida[8], _1_Resta_0_Sumar_salida);
  xor xor_12 (xor_12_out, B_salida[9], _1_Resta_0_Sumar_salida);
  xor xor_13 (xor_13_out, B_salida[10], _1_Resta_0_Sumar_salida);
  xor xor_14 (xor_14_out, B_salida[11], _1_Resta_0_Sumar_salida);
  xor xor_15 (xor_15_out, B_salida[12], _1_Resta_0_Sumar_salida);
  xor xor_16 (xor_16_out, B_salida[13], _1_Resta_0_Sumar_salida);
  xor xor_17 (xor_17_out, B_salida[14], _1_Resta_0_Sumar_salida);
  xor xor_18 (xor_18_out, B_salida[15], _1_Resta_0_Sumar_salida);
  SUMADOR_COMPLETO sumador_completo_1 (
    .A(_1_Resta_0_Sumar_salida), .B(A_salida[0]), .C(xor_3_out), .Acarreo(sumador_completo_1_acarreo),
    .Suma(sumador_completo_1_suma[0]));
  SUMADOR_COMPLETO sumador_completo_2 (
    .A(sumador_completo_1_acarreo), .B(A_salida[1]), .C(xor_4_out), .Acarreo(sumador_completo_2_acarreo),
    .Suma(sumador_completo_1_suma[1]));
  SUMADOR_COMPLETO sumador_completo_3 (
    .A(sumador_completo_2_acarreo), .B(A_salida[2]), .C(xor_5_out), .Acarreo(sumador_completo_3_acarreo),
    .Suma(sumador_completo_1_suma[2]));
  SUMADOR_COMPLETO sumador_completo_4 (
    .A(sumador_completo_3_acarreo), .B(A_salida[3]), .C(xor_6_out), .Acarreo(sumador_completo_4_acarreo),
    .Suma(sumador_completo_1_suma[3]));
  SUMADOR_COMPLETO sumador_completo_5 (
    .A(sumador_completo_4_acarreo), .B(A_salida[4]), .C(xor_7_out), .Acarreo(sumador_completo_5_acarreo),
    .Suma(sumador_completo_1_suma[4]));
  SUMADOR_COMPLETO sumador_completo_6 (
    .A(sumador_completo_5_acarreo), .B(A_salida[5]), .C(xor_8_out), .Acarreo(sumador_completo_6_acarreo),
    .Suma(sumador_completo_1_suma[5]));
  SUMADOR_COMPLETO sumador_completo_7 (
    .A(sumador_completo_6_acarreo), .B(A_salida[6]), .C(xor_9_out), .Acarreo(sumador_completo_7_acarreo),
    .Suma(sumador_completo_1_suma[6]));
  SUMADOR_COMPLETO sumador_completo_8 (
    .A(sumador_completo_7_acarreo), .B(A_salida[7]), .C(xor_10_out), .Acarreo(sumador_completo_8_acarreo),
    .Suma(sumador_completo_1_suma[7]));
  SUMADOR_COMPLETO sumador_completo_9 (
    .A(sumador_completo_8_acarreo), .B(A_salida[8]), .C(xor_11_out), .Acarreo(sumador_completo_9_acarreo),
    .Suma(sumador_completo_1_suma[8]));
  SUMADOR_COMPLETO sumador_completo_10 (
    .A(sumador_completo_9_acarreo), .B(A_salida[9]), .C(xor_12_out), .Acarreo(sumador_completo_10_acarreo),
    .Suma(sumador_completo_1_suma[9]));
  SUMADOR_COMPLETO sumador_completo_11 (
    .A(sumador_completo_10_acarreo), .B(A_salida[10]), .C(xor_13_out), .Acarreo(sumador_completo_11_acarreo),
    .Suma(sumador_completo_1_suma[10]));
  SUMADOR_COMPLETO sumador_completo_12 (
    .A(sumador_completo_11_acarreo), .B(A_salida[11]), .C(xor_14_out), .Acarreo(sumador_completo_12_acarreo),
    .Suma(sumador_completo_1_suma[11]));
  SUMADOR_COMPLETO sumador_completo_13 (
    .A(sumador_completo_12_acarreo), .B(A_salida[12]), .C(xor_15_out), .Acarreo(sumador_completo_13_acarreo),
    .Suma(sumador_completo_1_suma[12]));
  SUMADOR_COMPLETO sumador_completo_14 (
    .A(sumador_completo_13_acarreo), .B(A_salida[13]), .C(xor_16_out), .Acarreo(sumador_completo_14_acarreo),
    .Suma(sumador_completo_1_suma[13]));
  SUMADOR_COMPLETO sumador_completo_15 (
    .A(sumador_completo_14_acarreo), .B(A_salida[14]), .C(xor_17_out), .Acarreo(sumador_completo_15_acarreo),
    .Suma(sumador_completo_1_suma[14]));
  SUMADOR_COMPLETO sumador_completo_16 (
    .A(sumador_completo_15_acarreo), .B(A_salida[15]), .C(xor_18_out), .Acarreo(out_40),
    .Suma(sumador_completo_1_suma[15]));
  MULTI_B16 multi_b16_3 (
    .E0(sumador_completo_1_suma), .E1(C_A_salida), .SELECTOR(not_10_out), .ENABLE(1'b1), .SALIDA(C));
  Display display_1 (
    .in_1(C), ._11(display_1__11), ._1(display_1__1), ._1111(display_1__1111), ._111(display_1__111),
    ._22(display_1__22), ._2(display_1__2), ._2222(display_1__2222), ._222(display_1__222),
    ._33(display_1__33), ._3(display_1__3), ._3333(display_1__3333), ._333(display_1__333),
    ._44(display_1__44), ._4(display_1__4), ._4444(display_1__4444), ._444(display_1__444),
    ._55(display_1__55), ._5(display_1__5), ._5555(display_1__5555), ._555(display_1__555),
    ._66(display_1__66), ._6(display_1__6), ._6666(display_1__6666), ._666(display_1__666),
    ._77(display_1__77), ._7(display_1__7), ._7777(display_1__7777), ._777(display_1__777));
  _7_Segment_Display u_7_segment_display_1 (
    .g(display_1__7), .f(display_1__6), .a(display_1__1), .b(display_1__2), .e(display_1__5),
    .d(display_1__4), .c(display_1__3));  // open: dp
  _7_Segment_Display u_7_segment_display_2 (
    .g(display_1__77), .f(display_1__66), .a(display_1__11), .b(display_1__22), .e(display_1__55),
    .d(display_1__44), .c(display_1__33));  // open: dp
  _7_Segment_Display u_7_segment_display_3 (
    .g(display_1__777), .f(display_1__666), .a(display_1__111), .b(display_1__222), .e(display_1__555),
    .d(display_1__444), .c(display_1__333));  // open: dp
  _7_Segment_Display u_7_segment_display_4 (
    .g(display_1__7777), .f(display_1__6666), .a(display_1__1111), .b(display_1__2222), .e(display_1__5555),
    .d(display_1__4444), .c(display_1__3333));  // open: dp
endmodule

// SEM
module SEMI_SUMADOR (
  input  F,
  input  G,
  output I,
  output H
);

  xor xor_1 (H, F, G);
  and and_1 (I, F, G);
endmodule

// SUM-16
module SUMADOR_COMPLETO (
  input  A,
  input  B,
  input  C,
  output Suma,
  output Acarreo
);

  wire semi_sumador_1_h, semi_sumador_1_i, semi_sumador_2_i;

  SEMI_SUMADOR semi_sumador_1 (.F(B), .G(C), .I(semi_sumador_1_i), .H(semi_sumador_1_h));
  SEMI_SUMADOR semi_sumador_2 (.F(A), .G(semi_sumador_1_h), .I(semi_sumador_2_i), .H(Suma));
  or or_1 (Acarreo, semi_sumador_1_i, semi_sumador_2_i);
endmodule

// MUX-1
module MULTI_B1 (
  input  E0,
  input  E1,
  input  SELECTOR,
  input  ENABLE,
  output SALIDA
);

  wire and_1_out, and_2_out, not_1_out;

  not not_1 (not_1_out, SELECTOR);
  and and_1 (and_1_out, E0, ENABLE, not_1_out);
  and and_2 (and_2_out, E1, ENABLE, SELECTOR);
  or or_1 (SALIDA, and_1_out, and_2_out);
endmodule

// MUX-16
module MULTI_B16 (
  input  [15:0] E0,
  input  [15:0] E1,
  input  SELECTOR,
  input  ENABLE,
  output [15:0] SALIDA
);

  wire [15:0] and_1_out, and_2_out, bit_extender_1_out, bit_extender_2_out, not_1_out;

  assign not_1_out = ~bit_extender_1_out;  // NOT_Gate not_1, 16 bits wide
  assign bit_extender_1_out = {{15{SELECTOR}}, SELECTOR};  // Bit_Extender bit_extender_1
  assign bit_extender_2_out = {{15{ENABLE}}, ENABLE};  // Bit_Extender bit_extender_2
  assign and_1_out = E0 & bit_extender_2_out & not_1_out;  // AND_Gate and_1, 16 bits wide
  assign and_2_out = E1 & bit_extender_2_out & bit_extender_1_out;  // AND_Gate and_2, 16 bits wide
  assign SALIDA = and_1_out | and_2_out;  // OR_Gate or_1, 16 bits wide
endmodule

// CM-16
module COMPL_B16 (
  input  [15:0] in_1,
  output [15:0] out_2,
  output out_3
);

  wire not_1_out, not_2_out, not_3_out, not_4_out, not_5_out, not_6_out, not_7_out, not_8_out, not_9_out,
       not_10_out, not_11_out, not_12_out, not_13_out, not_14_out, not_15_out, not_16_out,
       sumador_completo_1_acarreo, sumador_completo_2_acarreo, sumador_completo_3_acarreo,
       sumador_completo_4_acarreo, sumador_completo_5_acarreo, sumador_completo_6_acarreo,
       sumador_completo_7_acarreo, sumador_completo_8_acarreo, sumador_completo_9_acarreo,
       sumador_completo_10_acarreo, sumador_completo_11_acarreo, sumador_completo_12_acarreo,
       sumador_completo_13_acarreo, sumador_completo_14_acarreo, sumador_completo_15_acarreo;

  not not_1 (not_1_out, in_1[0]);
  not not_2 (not_2_out, in_1[1]);
  not not_3 (not_3_out, in_1[2]);
  not not_4 (not_4_out, in_1[3]);
  not not_5 (not_5_out, in_1[4]);
  not not_6 (not_6_out, in_1[5]);
  not not_7 (not_7_out, in_1[6]);
  not not_8 (not_8_out, in_1[7]);
  not not_9 (not_9_out, in_1[8]);
  not not_10 (not_10_out, in_1[9]);
  not not_11 (not_11_out, in_1[10]);
  not not_12 (not_12_out, in_1[11]);
  not not_13 (not_13_out, in_1[12]);
  not not_14 (not_14_out, in_1[13]);
  not not_15 (not_15_out, in_1[14]);
  not not_16 (not_16_out, in_1[15]);
  SUMADOR_COMPLETO sumador_completo_1 (
    .A(1'b1), .B(not_1_out), .C(1'b0), .Acarreo(sumador_completo_1_acarreo), .Suma(out_2[0]));
  SUMADOR_COMPLETO sumador_completo_2 (
    .A(sumador_completo_1_acarreo), .B(not_2_out), .C(1'b0), .Acarreo(sumador_completo_2_acarreo),
    .Suma(out_2[1]));
  SUMADOR_COMPLETO sumador_completo_3 (
    .A(sumador_completo_2_acarreo), .B(not_3_out), .C(1'b0), .Acarreo(sumador_completo_3_acarreo),
    .Suma(out_2[2]));
  SUMADOR_COMPLETO sumador_completo_4 (
    .A(sumador_completo_3_acarreo), .B(not_4_out), .C(1'b0), .Acarreo(sumador_completo_4_acarreo),
    .Suma(out_2[3]));
  SUMADOR_COMPLETO sumador_completo_5 (
    .A(sumador_completo_4_acarreo), .B(not_5_out), .C(1'b0), .Acarreo(sumador_completo_5_acarreo),
    .Suma(out_2[4]));
  SUMADOR_COMPLETO sumador_completo_6 (
    .A(sumador_completo_5_acarreo), .B(not_6_out), .C(1'b0), .Acarreo(sumador_completo_6_acarreo),
    .Suma(out_2[5]));
  SUMADOR_COMPLETO sumador_completo_7 (
    .A(sumador_completo_6_acarreo), .B(not_7_out), .C(1'b0), .Acarreo(sumador_completo_7_acarreo),
    .Suma(out_2[6]));
  SUMADOR_COMPLETO sumador_completo_8 (
    .A(sumador_completo_7_acarreo), .B(not_8_out), .C(1'b0), .Acarreo(sumador_completo_8_acarreo),
    .Suma(out_2[7]));
  SUMADOR_COMPLETO sumador_completo_9 (
    .A(sumador_completo_8_acarreo), .B(not_9_out), .C(1'b0), .Acarreo(sumador_completo_9_acarreo),
    .Suma(out_2[8]));
  SUMADOR_COMPLETO sumador_completo_10 (
    .A(sumador_completo_9_acarreo), .B(not_10_out), .C(1'b0), .Acarreo(sumador_completo_10_acarreo),
    .Suma(out_2[9]));
  SUMADOR_COMPLETO sumador_completo_11 (
    .A(sumador_completo_10_acarreo), .B(not_11_out), .C(1'b0), .Acarreo(sumador_completo_11_acarreo),
    .Suma(out_2[10]));
  SUMADOR_COMPLETO sumador_completo_12 (
    .A(sumador_completo_11_acarreo), .B(not_12_out), .C(1'b0), .Acarreo(sumador_completo_12_acarreo),
    .Suma(out_2[11]));
  SUMADOR_COMPLETO sumador_completo_13 (
    .A(sumador_completo_12_acarreo), .B(not_13_out), .C(1'b0), .Acarreo(sumador_completo_13_acarreo),
    .Suma(out_2[12]));
  SUMADOR_COMPLETO sumador_completo_14 (
    .A(sumador_completo_13_acarreo), .B(not_14_out), .C(1'b0), .Acarreo(sumador_completo_14_acarreo),
    .Suma(out_2[13]));
  SUMADOR_COMPLETO sumador_completo_15 (
    .A(sumador_completo_14_acarreo), .B(not_15_out), .C(1'b0), .Acarreo(sumador_completo_15_acarreo),
    .Suma(out_2[14]));
  SUMADOR_COMPLETO sumador_completo_16 (
    .A(sumador_completo_15_acarreo), .B(not_16_out), .C(1'b0), .Acarreo(out_3), .Suma(out_2[15]));

  // Notes on the sheet:
  //   Sumamos 1 para realizar un corrido de digitos, de esta forma se obtiene el complemento 2
endmodule

// C-16
module COMP_B16 (
  input  [15:0] A,
  input  [15:0] B,
  output out_3,
  output out_4,
  output out_5
);

  wire comp_b1_1_out_4, comp_b1_2_out_4, comp_b4_1_out_4, comp_b4_1_out_5, comp_b4_2_out_4, comp_b4_2_out_5,
       comp_b4_3_out_4, comp_b4_3_out_5, comp_b4_4_out_4, comp_b4_4_out_5, comp_b16_2_1_out_12,
       comp_b16_2_1_out_14, xor_1_out;

  COMP_B4 comp_b4_1 (.in_1(A[3:0]), .in_2(B[3:0]), .out_4(comp_b4_1_out_4), .out_5(comp_b4_1_out_5));  // open: out_3
  COMP_B4 comp_b4_2 (.in_1(A[7:4]), .in_2(B[7:4]), .out_4(comp_b4_2_out_4), .out_5(comp_b4_2_out_5));  // open: out_3
  COMP_B4 comp_b4_3 (.in_1(A[11:8]), .in_2(B[11:8]), .out_4(comp_b4_3_out_4), .out_5(comp_b4_3_out_5));  // open: out_3
  COMP_B4 comp_b4_4 (
    .in_1(A[15:12]), .in_2(B[15:12]), .out_4(comp_b4_4_out_4), .out_5(comp_b4_4_out_5));  // open: out_3
  COMP_B1 comp_b1_1 (.in_1(1'b1), .in_2(A[15]), .out_4(comp_b1_1_out_4));  // open: out_3, out_5
  COMP_B1 comp_b1_2 (.in_1(1'b1), .in_2(B[15]), .out_4(comp_b1_2_out_4));  // open: out_3, out_5
  COMP_B16___2 comp_b16_2_1 (
    .A4(comp_b4_4_out_4), .B4(comp_b4_4_out_5), .A3(comp_b4_3_out_4), .B3(comp_b4_3_out_5), .in_5(1'b0),
    .in_6(1'b1), .in_7(1'b0), .A2(comp_b4_2_out_4), .B2(comp_b4_2_out_5), .A1(comp_b4_1_out_4),
    .B1(comp_b4_1_out_5), .out_12(comp_b16_2_1_out_12), .out_13(out_4), .out_14(comp_b16_2_1_out_14));
  xor xor_1 (xor_1_out, comp_b1_1_out_4, comp_b1_2_out_4);
  xor xor_2 (out_3, xor_1_out, comp_b16_2_1_out_12);
  xor xor_3 (out_5, comp_b16_2_1_out_14, xor_1_out);

  // Notes on the sheet:
  //   A partir de comparador de 4 bits v1 y v2(7485) se unen y se adaptan para que tambien se puedan comparar con números negativos
  //   Si A o B empiezan por 1, quiere decir que son números negativos
endmodule

// C-4
module COMP_B4 (
  input  [3:0] in_1,
  input  [3:0] in_2,
  output out_3,
  output out_4,
  output out_5
);

  wire and_1_out, and_2_out, and_3_out, and_4_out, and_5_out, and_6_out, and_7_out, and_8_out, and_9_out,
       and_10_out, and_11_out, and_12_out, and_13_out, and_14_out, nor_1_out, nor_2_out, nor_3_out,
       nor_4_out, not_1_out, not_2_out, not_3_out, not_4_out, not_5_out, not_6_out, not_7_out, not_8_out;

  not not_1 (not_1_out, in_1[0]);
  not not_2 (not_2_out, in_1[1]);
  not not_3 (not_3_out, in_2[0]);
  not not_4 (not_4_out, in_2[1]);
  not not_5 (not_5_out, in_1[2]);
  not not_6 (not_6_out, in_2[2]);
  not not_7 (not_7_out, in_1[3]);
  not not_8 (not_8_out, in_2[3]);
  and and_1 (and_1_out, not_1_out, in_2[0]);
  and and_2 (and_2_out, in_1[0], not_3_out);
  and and_3 (and_3_out, not_2_out, in_2[1]);
  and and_4 (and_4_out, in_1[1], not_4_out);
  and and_5 (and_5_out, not_5_out, in_2[2]);
  and and_6 (and_6_out, in_1[2], not_6_out);
  and and_7 (and_7_out, not_7_out, in_2[3]);
  and and_8 (and_8_out, in_1[3], not_8_out);
  nor nor_1 (nor_1_out, and_1_out, and_2_out);
  nor nor_2 (nor_2_out, and_3_out, and_4_out);
  nor nor_3 (nor_3_out, and_5_out, and_6_out);
  nor nor_4 (nor_4_out, and_7_out, and_8_out);
  and and_9 (and_9_out, and_1_out, nor_2_out, nor_3_out, nor_4_out);
  and and_10 (and_10_out, nor_2_out, nor_3_out, nor_4_out, and_2_out);
  and and_11 (and_11_out, and_3_out, nor_4_out, nor_3_out);
  and and_12 (and_12_out, nor_4_out, nor_4_out, and_4_out);
  and and_13 (and_13_out, and_5_out, nor_4_out);
  and and_14 (and_14_out, nor_4_out, and_6_out);
  and and_15 (out_3, nor_4_out, nor_3_out, nor_2_out, nor_1_out);
  or \or  (out_4, and_10_out, and_12_out, and_14_out, and_8_out);
  or or_2 (out_5, and_9_out, and_11_out, and_13_out, and_7_out);
endmodule

// C-4 V2
module COMP_B16___2 (
  input  A4,
  input  B4,
  input  A3,
  input  B3,
  input  in_5,
  input  in_6,
  input  in_7,
  input  A2,
  input  B2,
  input  A1,
  input  B1,
  output out_12,
  output out_13,
  output out_14
);

  wire and_1_out, and_2_out, and_3_out, and_4_out, and_5_out, and_6_out, and_7_out, and_8_out, and_9_out,
       and_10_out, and_11_out, and_12_out, and_13_out, and_14_out, and_16_out, and_17_out, and_18_out,
       and_19_out, and_20_out, and_21_out, nand_1_out, nand_2_out, nand_3_out, nand_4_out, nor_1_out,
       nor_2_out, nor_3_out, nor_4_out;

  nand nand_1 (nand_1_out, A4, B4);
  nand nand_2 (nand_2_out, A3, B3);
  nand nand_3 (nand_3_out, A2, B2);
  nand nand_4 (nand_4_out, A1, B1);
  and and_1 (and_1_out, A4, nand_1_out);
  and and_2 (and_2_out, nand_1_out, B4);
  and and_3 (and_3_out, A3, nand_2_out);
  and and_4 (and_4_out, nand_2_out, B3);
  and and_5 (and_5_out, A2, nand_3_out);
  and and_6 (and_6_out, nand_3_out, B2);
  and and_7 (and_7_out, A1, nand_4_out);
  and and_8 (and_8_out, nand_4_out, B1);
  nor nor_1 (nor_1_out, and_1_out, and_2_out);
  nor nor_2 (nor_2_out, and_3_out, and_4_out);
  nor nor_3 (nor_3_out, and_5_out, and_6_out);
  nor nor_4 (nor_4_out, and_7_out, and_8_out);
  and and_9 (and_9_out, B4, nand_1_out);
  and and_10 (and_10_out, B3, nand_2_out, nor_1_out);
  and and_11 (and_11_out, B2, nand_3_out, nor_1_out, nor_2_out);
  and and_12 (and_12_out, B1, nand_4_out, nor_1_out, nor_2_out, nor_3_out);
  and and_13 (and_13_out, nor_1_out, nor_2_out, nor_3_out, nor_4_out, in_5);
  and and_14 (and_14_out, nor_1_out, nor_2_out, nor_3_out, nor_4_out, in_6);
  and and_15 (out_13, nor_1_out, nor_2_out, in_6, nor_3_out, nor_4_out);
  and and_16 (and_16_out, in_6, nor_4_out, nor_3_out, nor_2_out, nor_1_out);
  and and_17 (and_17_out, in_7, nor_4_out, nor_3_out, nor_2_out, nor_1_out);
  and and_18 (and_18_out, nor_3_out, nor_2_out, nor_1_out, nand_4_out, A1);
  and and_19 (and_19_out, nor_2_out, nor_1_out, nand_3_out, A2);
  and and_20 (and_20_out, nor_1_out, nand_2_out, A3);
  and and_21 (and_21_out, nand_1_out, A4);
  nor nor_5 (out_12, and_9_out, and_10_out, and_11_out, and_12_out, and_13_out, and_14_out);
  nor nor_6 (out_14, and_16_out, and_17_out, and_18_out, and_19_out, and_20_out, and_21_out);
endmodule

// C-1
module COMP_B1 (
  input  in_1,
  input  in_2,
  output out_3,
  output out_4,
  output out_5
);

  wire not_1_out, not_2_out;

  not not_1 (not_1_out, in_2);
  not not_2 (not_2_out, in_1);
  and and_1 (out_3, in_1, not_1_out);
  and and_2 (out_5, not_2_out, in_2);
  nor nor_1 (out_4, out_3, out_5);
endmodule

// Display Hexa
module Display (
  input  [15:0] in_1,
  output _11,
  output _1,
  output _1111,
  output _111,
  output _22,
  output _2,
  output _2222,
  output _222,
  output _33,
  output _3,
  output _3333,
  output _333,
  output _44,
  output _4,
  output _4444,
  output _444,
  output _55,
  output _5,
  output _5555,
  output _555,
  output _66,
  output _6,
  output _6666,
  output _666,
  output _77,
  output _7,
  output _7777,
  output _777
);

  wire A_prime_B_2_out, A_prime_B_3_out, A_prime_B_4_out, A_prime_B_out, A_prime_B_prime_2_out,
       A_prime_B_prime_3_out, A_prime_B_prime_4_out, A_prime_B_prime_D_prime_2_out,
       A_prime_B_prime_D_prime_3_out, A_prime_B_prime_D_prime_4_out, A_prime_B_prime_D_prime_out,
       A_prime_B_prime_out, A_prime_BC_prime_2_out, A_prime_BC_prime_3_out, A_prime_BC_prime_4_out,
       A_prime_BC_prime_out, A_prime_BD_2_out, A_prime_BD_3_out, A_prime_BD_4_out, A_prime_BD_out,
       A_prime_C_2_out, A_prime_C_3_out, A_prime_C_4_out, A_prime_C_out, A_prime_C_prime_D_prime_2_out,
       A_prime_C_prime_D_prime_3_out, A_prime_C_prime_D_prime_4_out, A_prime_C_prime_D_prime_out,
       A_prime_CD_2_out, A_prime_CD_3_out, A_prime_CD_4_out, A_prime_CD_out, A_prime_CD_prime_2_out,
       A_prime_CD_prime_3_out, A_prime_CD_prime_4_out, A_prime_CD_prime_out, AB_2_out, AB_3_out, AB_4_out,
       AB_out, AB_prime_2_out, AB_prime_3_out, AB_prime_4_out, AB_prime_5_out, AB_prime_6_out,
       AB_prime_7_out, AB_prime_8_out, AB_prime_C_prime_2_out, AB_prime_C_prime_3_out,
       AB_prime_C_prime_4_out, AB_prime_C_prime_out, AB_prime_out, ABD_prime_2_out, ABD_prime_3_out,
       ABD_prime_4_out, ABD_prime_out, AC_2_out, AC_3_out, AC_4_out, AC_out, AC_prime_D_2_out,
       AC_prime_D_3_out, AC_prime_D_4_out, AC_prime_D_out, AC_prime_D_prime_2_out, AC_prime_D_prime_3_out,
       AC_prime_D_prime_4_out, AC_prime_D_prime_out, ACD_prime_2_out, ACD_prime_3_out, ACD_prime_4_out,
       ACD_prime_out, AD_2_out, AD_3_out, AD_4_out, AD_out, AD_prime_2_out, AD_prime_3_out, AD_prime_4_out,
       AD_prime_out, B_prime_C_2_out, B_prime_C_3_out, B_prime_C_4_out, B_prime_C_out, B_prime_C_prime_2_out,
       B_prime_C_prime_3_out, B_prime_C_prime_4_out, B_prime_C_prime_out, B_prime_CD_2_out, B_prime_CD_3_out,
       B_prime_CD_4_out, B_prime_CD_out, B_prime_D_2_out, B_prime_D_3_out, B_prime_D_4_out, B_prime_D_out,
       B_prime_D_prime_2_out, B_prime_D_prime_3_out, B_prime_D_prime_4_out, B_prime_D_prime_out, BC_2_out,
       BC_3_out, BC_4_out, BC_out, BC_prime_D_2_out, BC_prime_D_3_out, BC_prime_D_4_out, BC_prime_D_out,
       BD_prime_2_out, BD_prime_3_out, BD_prime_4_out, BD_prime_out, C_prime_D_2_out, C_prime_D_3_out,
       C_prime_D_4_out, C_prime_D_out, C_prime_D_prime_2_out, C_prime_D_prime_3_out, C_prime_D_prime_4_out,
       C_prime_D_prime_out, CD_prime_2_out, CD_prime_3_out, CD_prime_4_out, CD_prime_out, not_1_out,
       not_2_out, not_3_out, not_4_out, not_5_out, not_6_out, not_7_out, not_8_out, not_9_out, not_10_out,
       not_11_out, not_12_out, not_13_out, not_14_out, not_15_out, not_16_out;

  not not_1 (not_1_out, in_1[15]);
  not not_2 (not_2_out, in_1[14]);
  not not_3 (not_3_out, in_1[13]);
  not not_4 (not_4_out, in_1[12]);
  and B_prime_D_prime (B_prime_D_prime_out, not_2_out, not_4_out);
  and AB_prime_C_prime (AB_prime_C_prime_out, in_1[15], not_2_out, not_3_out);
  and AD_prime (AD_prime_out, in_1[15], not_4_out);
  and A_prime_BD (A_prime_BD_out, not_1_out, in_1[14], in_1[12]);
  and A_prime_C (A_prime_C_out, not_1_out, in_1[13]);
  and BC (BC_out, in_1[14], in_1[13]);
  and A_prime_B_prime (A_prime_B_prime_out, not_1_out, not_2_out);
  and B_prime_C_prime (B_prime_C_prime_out, not_2_out, not_3_out);
  and A_prime_C_prime_D_prime (A_prime_C_prime_D_prime_out, not_1_out, not_3_out, not_4_out);
  and A_prime_CD (A_prime_CD_out, not_1_out, in_1[13], in_1[12]);
  and ACD_prime (ACD_prime_out, in_1[15], in_1[13], not_4_out);
  and AC_prime_D (AC_prime_D_out, in_1[15], not_3_out, in_1[12]);
  and A_prime_B (A_prime_B_out, not_1_out, in_1[14]);
  and C_prime_D (C_prime_D_out, not_3_out, in_1[12]);
  and B_prime_D (B_prime_D_out, not_2_out, in_1[12]);
  and AB_prime (AB_prime_out, in_1[15], not_2_out);
  and BC_prime_D (BC_prime_D_out, in_1[14], not_3_out, in_1[12]);
  and ABD_prime (ABD_prime_out, in_1[15], in_1[14], not_4_out);
  and B_prime_CD (B_prime_CD_out, not_2_out, in_1[13], in_1[12]);
  and AC_prime_D_prime (AC_prime_D_prime_out, in_1[15], not_3_out, not_4_out);
  and A_prime_CD_prime (A_prime_CD_prime_out, not_1_out, in_1[13], not_4_out);
  and A_prime_B_prime_D_prime (A_prime_B_prime_D_prime_out, not_1_out, not_2_out, not_4_out);
  and AB (AB_out, in_1[15], in_1[14]);
  and CD_prime (CD_prime_out, in_1[13], not_4_out);
  and AC (AC_out, in_1[15], in_1[13]);
  and C_prime_D_prime (C_prime_D_prime_out, not_3_out, not_4_out);
  and A_prime_BC_prime (A_prime_BC_prime_out, not_1_out, in_1[14], not_3_out);
  and BD_prime (BD_prime_out, in_1[14], not_4_out);
  and AD (AD_out, in_1[15], in_1[12]);
  and AB_prime_2 (AB_prime_2_out, in_1[15], not_2_out);
  and B_prime_C (B_prime_C_out, not_2_out, in_1[13]);
  or a (_1, B_prime_D_prime_out, AB_prime_C_prime_out, AD_prime_out, A_prime_BD_out, A_prime_C_out, BC_out);
  or b (_2, A_prime_B_prime_out, B_prime_C_prime_out, A_prime_C_prime_D_prime_out, A_prime_CD_out, ACD_prime_out, AC_prime_D_out);
  or c (_3, B_prime_C_prime_out, A_prime_B_out, C_prime_D_out, B_prime_D_out, AB_prime_out);
  or d (_4, BC_prime_D_out, ABD_prime_out, B_prime_CD_out, AC_prime_D_prime_out, A_prime_CD_prime_out, A_prime_B_prime_D_prime_out);
  or e (_5, B_prime_D_prime_out, AB_out, CD_prime_out, AC_out);
  or f (_6, AC_out, AB_prime_out, C_prime_D_prime_out, A_prime_BC_prime_out, BD_prime_out);
  or g (_7, CD_prime_out, A_prime_BC_prime_out, AD_out, AB_prime_2_out, B_prime_C_out);
  _7_Segment_Display u_7_segment_display_1 (.g(_7), .f(_6), .a(_1), .b(_2), .e(_5), .d(_4), .c(_3));  // open: dp
  not not_5 (not_5_out, in_1[11]);
  _7_Segment_Display u_7_segment_display_2 (.g(_77), .f(_66), .a(_11), .b(_22), .e(_55), .d(_44), .c(_33));  // open: dp
  not not_6 (not_6_out, in_1[10]);
  not not_7 (not_7_out, in_1[9]);
  not not_8 (not_8_out, in_1[8]);
  and B_prime_D_prime_2 (B_prime_D_prime_2_out, not_6_out, not_8_out);
  and AB_prime_C_prime_2 (AB_prime_C_prime_2_out, in_1[11], not_6_out, not_7_out);
  and AD_prime_2 (AD_prime_2_out, in_1[11], not_8_out);
  and A_prime_BD_2 (A_prime_BD_2_out, not_5_out, in_1[10], in_1[8]);
  and A_prime_C_2 (A_prime_C_2_out, not_5_out, in_1[9]);
  and BC_2 (BC_2_out, in_1[10], in_1[9]);
  and A_prime_B_prime_2 (A_prime_B_prime_2_out, not_5_out, not_6_out);
  and B_prime_C_prime_2 (B_prime_C_prime_2_out, not_6_out, not_7_out);
  and A_prime_C_prime_D_prime_2 (A_prime_C_prime_D_prime_2_out, not_5_out, not_7_out, not_8_out);
  and A_prime_CD_2 (A_prime_CD_2_out, not_5_out, in_1[9], in_1[8]);
  and ACD_prime_2 (ACD_prime_2_out, in_1[11], in_1[9], not_8_out);
  and AC_prime_D_2 (AC_prime_D_2_out, in_1[11], not_7_out, in_1[8]);
  and A_prime_B_2 (A_prime_B_2_out, not_5_out, in_1[10]);
  and C_prime_D_2 (C_prime_D_2_out, not_7_out, in_1[8]);
  and B_prime_D_2 (B_prime_D_2_out, not_6_out, in_1[8]);
  and AB_prime_3 (AB_prime_3_out, in_1[11], not_6_out);
  and BC_prime_D_2 (BC_prime_D_2_out, in_1[10], not_7_out, in_1[8]);
  and ABD_prime_2 (ABD_prime_2_out, in_1[11], in_1[10], not_8_out);
  and B_prime_CD_2 (B_prime_CD_2_out, not_6_out, in_1[9], in_1[8]);
  and AC_prime_D_prime_2 (AC_prime_D_prime_2_out, in_1[11], not_7_out, not_8_out);
  and A_prime_CD_prime_2 (A_prime_CD_prime_2_out, not_5_out, in_1[9], not_8_out);
  and A_prime_B_prime_D_prime_2 (A_prime_B_prime_D_prime_2_out, not_5_out, not_6_out, not_8_out);
  and AB_2 (AB_2_out, in_1[11], in_1[10]);
  and CD_prime_2 (CD_prime_2_out, in_1[9], not_8_out);
  and AC_2 (AC_2_out, in_1[11], in_1[9]);
  and C_prime_D_prime_2 (C_prime_D_prime_2_out, not_7_out, not_8_out);
  and A_prime_BC_prime_2 (A_prime_BC_prime_2_out, not_5_out, in_1[10], not_7_out);
  and BD_prime_2 (BD_prime_2_out, in_1[10], not_8_out);
  and AD_2 (AD_2_out, in_1[11], in_1[8]);
  and AB_prime_4 (AB_prime_4_out, in_1[11], not_6_out);
  and B_prime_C_2 (B_prime_C_2_out, not_6_out, in_1[9]);
  or a_2 (_11, B_prime_D_prime_2_out, AB_prime_C_prime_2_out, AD_prime_2_out, A_prime_BD_2_out, A_prime_C_2_out, BC_2_out);
  or b_2 (_22, A_prime_B_prime_2_out, B_prime_C_prime_2_out, A_prime_C_prime_D_prime_2_out, A_prime_CD_2_out, ACD_prime_2_out, AC_prime_D_2_out);
  or c_2 (_33, B_prime_C_prime_2_out, A_prime_B_2_out, C_prime_D_2_out, B_prime_D_2_out, AB_prime_3_out);
  or d_2 (_44, BC_prime_D_2_out, ABD_prime_2_out, B_prime_CD_2_out, AC_prime_D_prime_2_out, A_prime_CD_prime_2_out, A_prime_B_prime_D_prime_2_out);
  or e_2 (_55, B_prime_D_prime_2_out, AB_2_out, CD_prime_2_out, AC_2_out);
  or f_2 (_66, AC_2_out, AB_prime_3_out, C_prime_D_prime_2_out, A_prime_BC_prime_2_out, BD_prime_2_out);
  or g_2 (_77, CD_prime_2_out, A_prime_BC_prime_2_out, AD_2_out, AB_prime_4_out, B_prime_C_2_out);
  _7_Segment_Display u_7_segment_display_3 (
    .g(_777), .f(_666), .a(_111), .b(_222), .e(_555), .d(_444), .c(_333));  // open: dp
  not not_9 (not_9_out, in_1[7]);
  not not_10 (not_10_out, in_1[6]);
  not not_11 (not_11_out, in_1[5]);
  not not_12 (not_12_out, in_1[4]);
  and B_prime_D_prime_3 (B_prime_D_prime_3_out, not_10_out, not_12_out);
  and AB_prime_C_prime_3 (AB_prime_C_prime_3_out, in_1[7], not_10_out, not_11_out);
  and AD_prime_3 (AD_prime_3_out, in_1[7], not_12_out);
  and A_prime_BD_3 (A_prime_BD_3_out, not_9_out, in_1[6], in_1[4]);
  and A_prime_C_3 (A_prime_C_3_out, not_9_out, in_1[5]);
  and BC_3 (BC_3_out, in_1[6], in_1[5]);
  and A_prime_B_prime_3 (A_prime_B_prime_3_out, not_9_out, not_10_out);
  and B_prime_C_prime_3 (B_prime_C_prime_3_out, not_10_out, not_11_out);
  and A_prime_C_prime_D_prime_3 (A_prime_C_prime_D_prime_3_out, not_9_out, not_11_out, not_12_out);
  and A_prime_CD_3 (A_prime_CD_3_out, not_9_out, in_1[5], in_1[4]);
  and ACD_prime_3 (ACD_prime_3_out, in_1[7], in_1[5], not_12_out);
  and AC_prime_D_3 (AC_prime_D_3_out, in_1[7], not_11_out, in_1[4]);
  and A_prime_B_3 (A_prime_B_3_out, not_9_out, in_1[6]);
  and C_prime_D_3 (C_prime_D_3_out, not_11_out, in_1[4]);
  and B_prime_D_3 (B_prime_D_3_out, not_10_out, in_1[4]);
  and AB_prime_5 (AB_prime_5_out, in_1[7], not_10_out);
  and BC_prime_D_3 (BC_prime_D_3_out, in_1[6], not_11_out, in_1[4]);
  and ABD_prime_3 (ABD_prime_3_out, in_1[7], in_1[6], not_12_out);
  and B_prime_CD_3 (B_prime_CD_3_out, not_10_out, in_1[5], in_1[4]);
  and AC_prime_D_prime_3 (AC_prime_D_prime_3_out, in_1[7], not_11_out, not_12_out);
  and A_prime_CD_prime_3 (A_prime_CD_prime_3_out, not_9_out, in_1[5], not_12_out);
  and A_prime_B_prime_D_prime_3 (A_prime_B_prime_D_prime_3_out, not_9_out, not_10_out, not_12_out);
  and AB_3 (AB_3_out, in_1[7], in_1[6]);
  and CD_prime_3 (CD_prime_3_out, in_1[5], not_12_out);
  and AC_3 (AC_3_out, in_1[7], in_1[5]);
  and C_prime_D_prime_3 (C_prime_D_prime_3_out, not_11_out, not_12_out);
  and A_prime_BC_prime_3 (A_prime_BC_prime_3_out, not_9_out, in_1[6], not_11_out);
  and BD_prime_3 (BD_prime_3_out, in_1[6], not_12_out);
  and AD_3 (AD_3_out, in_1[7], in_1[4]);
  and AB_prime_6 (AB_prime_6_out, in_1[7], not_10_out);
  and B_prime_C_3 (B_prime_C_3_out, not_10_out, in_1[5]);
  or a_3 (_111, B_prime_D_prime_3_out, AB_prime_C_prime_3_out, AD_prime_3_out, A_prime_BD_3_out, A_prime_C_3_out, BC_3_out);
  or b_3 (_222, A_prime_B_prime_3_out, B_prime_C_prime_3_out, A_prime_C_prime_D_prime_3_out, A_prime_CD_3_out, ACD_prime_3_out, AC_prime_D_3_out);
  or c_3 (_333, B_prime_C_prime_3_out, A_prime_B_3_out, C_prime_D_3_out, B_prime_D_3_out, AB_prime_5_out);
  or d_3 (_444, BC_prime_D_3_out, ABD_prime_3_out, B_prime_CD_3_out, AC_prime_D_prime_3_out, A_prime_CD_prime_3_out, A_prime_B_prime_D_prime_3_out);
  or e_3 (_555, B_prime_D_prime_3_out, AB_3_out, CD_prime_3_out, AC_3_out);
  or f_3 (_666, AC_3_out, AB_prime_5_out, C_prime_D_prime_3_out, A_prime_BC_prime_3_out, BD_prime_3_out);
  or g_3 (_777, CD_prime_3_out, A_prime_BC_prime_3_out, AD_3_out, AB_prime_6_out, B_prime_C_3_out);
  not not_13 (not_13_out, in_1[3]);
  _7_Segment_Display u_7_segment_display_4 (
    .g(_7777), .f(_6666), .a(_1111), .b(_2222), .e(_5555), .d(_4444), .c(_3333));  // open: dp
  not not_14 (not_14_out, in_1[2]);
  not not_15 (not_15_out, in_1[1]);
  not not_16 (not_16_out, in_1[0]);
  and B_prime_D_prime_4 (B_prime_D_prime_4_out, not_14_out, not_16_out);
  and AB_prime_C_prime_4 (AB_prime_C_prime_4_out, in_1[3], not_14_out, not_15_out);
  and AD_prime_4 (AD_prime_4_out, in_1[3], not_16_out);
  and A_prime_BD_4 (A_prime_BD_4_out, not_13_out, in_1[2], in_1[0]);
  and A_prime_C_4 (A_prime_C_4_out, not_13_out, in_1[1]);
  and BC_4 (BC_4_out, in_1[2], in_1[1]);
  and A_prime_B_prime_4 (A_prime_B_prime_4_out, not_13_out, not_14_out);
  and B_prime_C_prime_4 (B_prime_C_prime_4_out, not_14_out, not_15_out);
  and A_prime_C_prime_D_prime_4 (A_prime_C_prime_D_prime_4_out, not_13_out, not_15_out, not_16_out);
  and A_prime_CD_4 (A_prime_CD_4_out, not_13_out, in_1[1], in_1[0]);
  and ACD_prime_4 (ACD_prime_4_out, in_1[3], in_1[1], not_16_out);
  and AC_prime_D_4 (AC_prime_D_4_out, in_1[3], not_15_out, in_1[0]);
  and A_prime_B_4 (A_prime_B_4_out, not_13_out, in_1[2]);
  and C_prime_D_4 (C_prime_D_4_out, not_15_out, in_1[0]);
  and B_prime_D_4 (B_prime_D_4_out, not_14_out, in_1[0]);
  and AB_prime_7 (AB_prime_7_out, in_1[3], not_14_out);
  and BC_prime_D_4 (BC_prime_D_4_out, in_1[2], not_15_out, in_1[0]);
  and ABD_prime_4 (ABD_prime_4_out, in_1[3], in_1[2], not_16_out);
  and B_prime_CD_4 (B_prime_CD_4_out, not_14_out, in_1[1], in_1[0]);
  and AC_prime_D_prime_4 (AC_prime_D_prime_4_out, in_1[3], not_15_out, not_16_out);
  and A_prime_CD_prime_4 (A_prime_CD_prime_4_out, not_13_out, in_1[1], not_16_out);
  and A_prime_B_prime_D_prime_4 (A_prime_B_prime_D_prime_4_out, not_13_out, not_14_out, not_16_out);
  and AB_4 (AB_4_out, in_1[3], in_1[2]);
  and CD_prime_4 (CD_prime_4_out, in_1[1], not_16_out);
  and AC_4 (AC_4_out, in_1[3], in_1[1]);
  and C_prime_D_prime_4 (C_prime_D_prime_4_out, not_15_out, not_16_out);
  and A_prime_BC_prime_4 (A_prime_BC_prime_4_out, not_13_out, in_1[2], not_15_out);
  and BD_prime_4 (BD_prime_4_out, in_1[2], not_16_out);
  and AD_4 (AD_4_out, in_1[3], in_1[0]);
  and AB_prime_8 (AB_prime_8_out, in_1[3], not_14_out);
  and B_prime_C_4 (B_prime_C_4_out, not_14_out, in_1[1]);
  or a_4 (_1111, B_prime_D_prime_4_out, AB_prime_C_prime_4_out, AD_prime_4_out, A_prime_BD_4_out, A_prime_C_4_out, BC_4_out);
  or b_4 (_2222, A_prime_B_prime_4_out, B_prime_C_prime_4_out, A_prime_C_prime_D_prime_4_out, A_prime_CD_4_out, ACD_prime_4_out, AC_prime_D_4_out);
  or c_4 (_3333, B_prime_C_prime_4_out, A_prime_B_4_out, C_prime_D_4_out, B_prime_D_4_out, AB_prime_7_out);
  or d_4 (_4444, BC_prime_D_4_out, ABD_prime_4_out, B_prime_CD_4_out, AC_prime_D_prime_4_out, A_prime_CD_prime_4_out, A_prime_B_prime_D_prime_4_out);
  or e_4 (_5555, B_prime_D_prime_4_out, AB_4_out, CD_prime_4_out, AC_4_out);
  or f_4 (_6666, AC_4_out, AB_prime_7_out, C_prime_D_prime_4_out, A_prime_BC_prime_4_out, BD_prime_4_out);
  or g_4 (_7777, CD_prime_4_out, A_prime_BC_prime_4_out, AD_4_out, AB_prime_8_out, B_prime_C_4_out);
endmodule
