// Logisim project Ping_Pong.circ as structural Verilog: 4 circuits, main circuit main
module main (
  input  _1__Borrar__Barra__0__No_borrar_barra,
  input  \_1__Generar_Posición_al_azar_0__No_generar_más_posiciones_al_azar ,
  input  _1_Para_pausar
);

  wire Crear_Barra_out, Iniciar_out, joy_1_n;
  wire [1:0] joy_1_out_5, joystick_1_x, joystick_1_y;
  wire [4:0] BPosC;
  wire [31:0] _3, _4, _5, _6, _7, _8, _9, _10, _11, _12, _13, _14, _15, _16, _17, _18, _19, _20, _21, _22,
       _23, _24, _25, _26, _27, _28, _29, _30, _31, _111, _222, DBC, en;

  Joystick #(.bits(2)) joystick_1 (.x(joystick_1_x), .y(joystick_1_y));
  Joy joy_1 (
    .A(joystick_1_x[1]), .B(joystick_1_x[0]), .C(joystick_1_y[1]), .D(joystick_1_y[0]), .out_5(joy_1_out_5),
    .N(joy_1_n));
  Button Crear_Barra (.out(Crear_Barra_out));
  Barra barra_1 (
    .A(Crear_Barra_out), .D(joy_1_out_5), .r(joy_1_n), .DIR(_1__Borrar__Barra__0__No_borrar_barra),
    .Fila_32(en));
  Button Iniciar (.out(Iniciar_out));
  Mov mov_1 (
    .Barra(en), .Reiniciar(Iniciar_out),
    .iniciar(\_1__Generar_Posición_al_azar_0__No_generar_más_posiciones_al_azar ), .Pausar(_1_Para_pausar),
    .BolaPosCol(BPosC), .DataBolaCol(DBC));
  DotMatrix #(.inputtype("row"), .matrixcols(32), .matrixrows(32)) dotmatrix_1 (
    .row0(_31), .row1(_30), .row2(_29), .row3(_28), .row4(_27), .row5(_26), .row6(_25), .row7(_24),
    .row8(_23), .row9(_22), .row10(_21), .row11(_20), .row12(_19), .row13(_18), .row14(_17), .row15(_16),
    .row16(_15), .row17(_14), .row18(_13), .row19(_12), .row20(_111), .row21(_10), .row22(_9), .row23(_8),
    .row24(_7), .row25(_6), .row26(_5), .row27(_4), .row28(_3), .row29(_222), .row30(_11), .row31(en));
  Demultiplexer #(.select(5), .width(32), .enable("false")) demultiplexer_1 (
    .out1(_11), .out2(_222), .out3(_3), .out4(_4), .out5(_5), .out6(_6), .out7(_7), .out8(_8), .out9(_9),
    .out10(_10), .out11(_111), .out12(_12), .out13(_13), .out14(_14), .out15(_15), .out16(_16), .out17(_17),
    .out18(_18), .out19(_19), .out20(_20), .out21(_21), .out22(_22), .out23(_23), .out24(_24), .out25(_25),
    .out26(_26), .out27(_27), .out28(_28), .out29(_29), .out30(_30), .out31(_31), .in(DBC), .sel(BPosC));  // open: out0

  // Notes on the sheet:
  //   Como usarlo:
  //   1. Crea la barra
  //   2. Selecciona la frecuencia a jugar. Se recomienda 4Hz - 8Hz - 16Hz
  //   3. Genera una posición al azar para la pelota (No dejes el botón en 1 todo el tiempo)
  //   4. Presiona Iniciar
  //   5. Usa el Joysitck para moverte horizontalmente
  //   Tambien puedes con varias barras a la vez
  //   Para borrar la barra, debes poner el botón en 1, mover el joystick y denuevo pones el boton en 0
endmodule

module Joy (
  input  A,
  input  B,
  input  C,
  input  D,
  output [1:0] out_5,
  output N
);

  wire and_5_out, not_1_out, not_2_out, not_3_out, not_4_out, not_5_out, not_6_out;
  wire [3:0] and_1_out;

  not not_1 (not_1_out, A);
  and and_1 (and_1_out[0], not_1_out, B, D);
  not not_2 (not_2_out, A);
  and and_2 (and_1_out[1], not_2_out, B, C);
  and and_3 (and_1_out[2], A, B, D);
  and and_4 (and_1_out[3], A, B, C);
  not not_3 (not_3_out, B);
  not not_4 (not_4_out, C);
  and and_5 (and_5_out, not_4_out, not_5_out);
  not not_5 (not_5_out, D);
  or or_1 (N, not_3_out, and_5_out);
  Multiplexer #(.select(4), .width(2)) multiplexer_1 (
    .in1(2'b01), .in2(2'b01), .in3(2'b01), .in4(2'b00), .in8(2'b00), .in12(2'b00), .out(out_5),
    .sel(and_1_out), .en(not_6_out));  // open: in0, in5, in6, in7, in9, in10, in11, in13, in14, in15
  not not_6 (not_6_out, N);
endmodule

module Barra (
  input  A,
  input  [1:0] D,
  input  r,
  input  DIR,
  output [31:0] Fila_32
);

  wire C_out, CLK, multiplexer_2_out, multiplexer_3_out, multiplexer_5_out, multiplexer_6_out,
       multiplexer_7_out, multiplexer_8_out, multiplexer_9_out, multiplexer_10_out, multiplexer_11_out,
       multiplexer_12_out, multiplexer_13_out, multiplexer_14_out, multiplexer_15_out, multiplexer_16_out,
       multiplexer_17_out, multiplexer_18_out, multiplexer_19_out, multiplexer_20_out, multiplexer_21_out,
       multiplexer_22_out, multiplexer_23_out, multiplexer_24_out, multiplexer_25_out, multiplexer_26_out,
       multiplexer_27_out, multiplexer_28_out, multiplexer_29_out, multiplexer_30_out, multiplexer_31_out,
       multiplexer_32_out, multiplexer_33_out, multiplexer_34_out;
  wire [1:0] DIR_t;

  Clock C (.out(C_out));
  Multiplexer #(.enable("false")) multiplexer_1 (.in0(C_out), .in1(1'b0), .out(CLK), .sel(r));
  Multiplexer #(.select(2), .enable("false")) multiplexer_2 (
    .in0(Fila_32[0]), .in1(Fila_32[30]), .in2(1'b0), .out(multiplexer_2_out), .sel(DIR_t));  // open: in3
  Multiplexer #(.select(2), .enable("false")) multiplexer_3 (
    .in0(Fila_32[12]), .in1(Fila_32[10]), .in2(1'b0), .out(multiplexer_3_out), .sel(DIR_t));  // open: in3
  Multiplexer #(.width(2), .enable("false")) multiplexer_4 (.in0(D), .in1(2'b10), .out(DIR_t), .sel(DIR));
  D_Flip_Flop d_ff_1 (.clk(CLK), .D(multiplexer_2_out), .Q(Fila_32[31]));  // open: Qn, preset, en, reset
  D_Flip_Flop d_ff_2 (.clk(CLK), .D(multiplexer_3_out), .Q(Fila_32[11]));  // open: Qn, preset, en, reset
  Multiplexer #(.select(2), .enable("false")) multiplexer_5 (
    .in0(Fila_32[31]), .in1(Fila_32[29]), .in2(1'b0), .out(multiplexer_5_out), .sel(DIR_t));  // open: in3
  Multiplexer #(.select(2), .enable("false")) multiplexer_6 (
    .in0(Fila_32[11]), .in1(Fila_32[9]), .in2(1'b0), .out(multiplexer_6_out), .sel(DIR_t));  // open: in3
  D_Flip_Flop d_ff_3 (.clk(CLK), .D(multiplexer_5_out), .Q(Fila_32[30]));  // open: Qn, preset, en, reset
  D_Flip_Flop d_ff_4 (.clk(CLK), .D(multiplexer_6_out), .Q(Fila_32[10]));  // open: Qn, preset, en, reset
  Multiplexer #(.select(2), .enable("false")) multiplexer_7 (
    .in0(Fila_32[30]), .in1(Fila_32[28]), .in2(1'b0), .out(multiplexer_7_out), .sel(DIR_t));  // open: in3
  Multiplexer #(.select(2), .enable("false")) multiplexer_8 (
    .in0(Fila_32[10]), .in1(Fila_32[8]), .in2(1'b0), .out(multiplexer_8_out), .sel(DIR_t));  // open: in3
  D_Flip_Flop d_ff_5 (.clk(CLK), .D(multiplexer_7_out), .Q(Fila_32[29]));  // open: Qn, preset, en, reset
  D_Flip_Flop d_ff_6 (.clk(CLK), .D(multiplexer_8_out), .Q(Fila_32[9]));  // open: Qn, preset, en, reset
  Multiplexer #(.select(2), .enable("false")) multiplexer_9 (
    .in0(Fila_32[29]), .in1(Fila_32[27]), .in2(1'b0), .out(multiplexer_9_out), .sel(DIR_t));  // open: in3
  Multiplexer #(.select(2), .enable("false")) multiplexer_10 (
    .in0(Fila_32[9]), .in1(Fila_32[7]), .in2(1'b0), .out(multiplexer_10_out), .sel(DIR_t));  // open: in3
  D_Flip_Flop d_ff_7 (.clk(CLK), .D(multiplexer_9_out), .Q(Fila_32[28]));  // open: Qn, preset, en, reset
  D_Flip_Flop d_ff_8 (.clk(CLK), .D(multiplexer_10_out), .Q(Fila_32[8]));  // open: Qn, preset, en, reset
  Multiplexer #(.select(2), .enable("false")) multiplexer_11 (
    .in0(Fila_32[28]), .in1(Fila_32[26]), .in2(1'b0), .out(multiplexer_11_out), .sel(DIR_t));  // open: in3
  Multiplexer #(.select(2), .enable("false")) multiplexer_12 (
    .in0(Fila_32[8]), .in1(Fila_32[6]), .in2(1'b0), .out(multiplexer_12_out), .sel(DIR_t));  // open: in3
  D_Flip_Flop d_ff_9 (.clk(CLK), .D(multiplexer_11_out), .Q(Fila_32[27]));  // open: Qn, preset, en, reset
  D_Flip_Flop d_ff_10 (.clk(CLK), .D(multiplexer_12_out), .Q(Fila_32[7]));  // open: Qn, preset, en, reset
  Multiplexer #(.select(2), .enable("false")) multiplexer_13 (
    .in0(Fila_32[27]), .in1(Fila_32[25]), .in2(1'b0), .out(multiplexer_13_out), .sel(DIR_t));  // open: in3
  Multiplexer #(.select(2), .enable("false")) multiplexer_14 (
    .in0(Fila_32[7]), .in1(Fila_32[5]), .in2(1'b0), .out(multiplexer_14_out), .sel(DIR_t));  // open: in3
  D_Flip_Flop d_ff_11 (.clk(CLK), .D(multiplexer_13_out), .Q(Fila_32[26]));  // open: Qn, preset, en, reset
  D_Flip_Flop d_ff_12 (.clk(CLK), .D(multiplexer_14_out), .Q(Fila_32[6]));  // open: Qn, preset, en, reset
  Multiplexer #(.select(2), .enable("false")) multiplexer_15 (
    .in0(Fila_32[26]), .in1(Fila_32[24]), .in2(1'b0), .out(multiplexer_15_out), .sel(DIR_t));  // open: in3
  Multiplexer #(.select(2), .enable("false")) multiplexer_16 (
    .in0(Fila_32[6]), .in1(Fila_32[4]), .in2(1'b0), .out(multiplexer_16_out), .sel(DIR_t));  // open: in3
  D_Flip_Flop d_ff_13 (.clk(CLK), .D(multiplexer_15_out), .Q(Fila_32[25]));  // open: Qn, preset, en, reset
  D_Flip_Flop d_ff_14 (.clk(CLK), .D(multiplexer_16_out), .Q(Fila_32[5]));  // open: Qn, preset, en, reset
  Multiplexer #(.select(2), .enable("false")) multiplexer_17 (
    .in0(Fila_32[25]), .in1(Fila_32[23]), .in2(1'b0), .out(multiplexer_17_out), .sel(DIR_t));  // open: in3
  D_Flip_Flop d_ff_15 (.clk(CLK), .D(multiplexer_17_out), .Q(Fila_32[24]));  // open: Qn, preset, en, reset
  Multiplexer #(.select(2), .enable("false")) multiplexer_18 (
    .in0(Fila_32[5]), .in1(Fila_32[3]), .in2(1'b0), .out(multiplexer_18_out), .sel(DIR_t));  // open: in3
  D_Flip_Flop d_ff_16 (.clk(CLK), .D(multiplexer_18_out), .Q(Fila_32[4]));  // open: Qn, preset, en, reset
  Multiplexer #(.select(2), .enable("false")) multiplexer_19 (
    .in0(Fila_32[24]), .in1(Fila_32[22]), .in2(1'b0), .out(multiplexer_19_out), .sel(DIR_t));  // open: in3
  Multiplexer #(.select(2), .enable("false")) multiplexer_20 (
    .in0(Fila_32[4]), .in1(Fila_32[2]), .in2(1'b0), .out(multiplexer_20_out), .sel(DIR_t));  // open: in3
  D_Flip_Flop d_ff_17 (.clk(CLK), .D(multiplexer_19_out), .Q(Fila_32[23]));  // open: Qn, preset, en, reset
  D_Flip_Flop d_ff_18 (.clk(CLK), .D(multiplexer_20_out), .Q(Fila_32[3]));  // open: Qn, preset, en, reset
  Multiplexer #(.select(2), .enable("false")) multiplexer_21 (
    .in0(Fila_32[23]), .in1(Fila_32[21]), .in2(1'b0), .out(multiplexer_21_out), .sel(DIR_t));  // open: in3
  Multiplexer #(.select(2), .enable("false")) multiplexer_22 (
    .in0(Fila_32[3]), .in1(Fila_32[1]), .in2(1'b0), .out(multiplexer_22_out), .sel(DIR_t));  // open: in3
  D_Flip_Flop d_ff_19 (.clk(CLK), .D(multiplexer_21_out), .Q(Fila_32[22]));  // open: Qn, preset, en, reset
  D_Flip_Flop d_ff_20 (.clk(CLK), .D(multiplexer_22_out), .Q(Fila_32[2]));  // open: Qn, preset, en, reset
  Multiplexer #(.select(2), .enable("false")) multiplexer_23 (
    .in0(Fila_32[22]), .in1(Fila_32[20]), .in2(1'b0), .out(multiplexer_23_out), .sel(DIR_t));  // open: in3
  Multiplexer #(.select(2), .enable("false")) multiplexer_24 (
    .in0(Fila_32[2]), .in1(Fila_32[0]), .in2(1'b0), .out(multiplexer_24_out), .sel(DIR_t));  // open: in3
  D_Flip_Flop d_ff_21 (.clk(CLK), .D(multiplexer_23_out), .Q(Fila_32[21]));  // open: Qn, preset, en, reset
  D_Flip_Flop d_ff_22 (.clk(CLK), .D(multiplexer_24_out), .Q(Fila_32[1]));  // open: Qn, preset, en, reset
  Multiplexer #(.select(2), .enable("false")) multiplexer_25 (
    .in0(Fila_32[21]), .in1(Fila_32[19]), .in2(1'b0), .out(multiplexer_25_out), .sel(DIR_t));  // open: in3
  Multiplexer #(.select(2), .enable("false")) multiplexer_26 (
    .in0(Fila_32[1]), .in1(Fila_32[31]), .in2(1'b0), .out(multiplexer_26_out), .sel(DIR_t));  // open: in3
  D_Flip_Flop d_ff_23 (.clk(CLK), .D(multiplexer_25_out), .Q(Fila_32[20]));  // open: Qn, preset, en, reset
  D_Flip_Flop d_ff_24 (.clk(CLK), .D(multiplexer_26_out), .Q(Fila_32[0]));  // open: Qn, preset, en, reset
  Multiplexer #(.select(2), .enable("false")) multiplexer_27 (
    .in0(Fila_32[20]), .in1(Fila_32[18]), .in2(1'b0), .out(multiplexer_27_out), .sel(DIR_t));  // open: in3
  D_Flip_Flop d_ff_25 (.clk(CLK), .D(multiplexer_27_out), .Q(Fila_32[19]));  // open: Qn, preset, en, reset
  Multiplexer #(.select(2), .enable("false")) multiplexer_28 (
    .in0(Fila_32[19]), .in1(Fila_32[17]), .in2(1'b0), .out(multiplexer_28_out), .sel(DIR_t));  // open: in3
  D_Flip_Flop d_ff_26 (.clk(CLK), .D(multiplexer_28_out), .Q(Fila_32[18]));  // open: Qn, preset, en, reset
  Multiplexer #(.select(2), .enable("false")) multiplexer_29 (
    .in0(Fila_32[18]), .in1(Fila_32[16]), .in2(1'b0), .out(multiplexer_29_out), .sel(DIR_t));  // open: in3
  D_Flip_Flop d_ff_27 (.clk(CLK), .D(multiplexer_29_out), .Q(Fila_32[17]), .preset(A));  // open: Qn, en, reset
  Multiplexer #(.select(2), .enable("false")) multiplexer_30 (
    .in0(Fila_32[17]), .in1(Fila_32[15]), .in2(1'b0), .out(multiplexer_30_out), .sel(DIR_t));  // open: in3
  D_Flip_Flop d_ff_28 (.clk(CLK), .D(multiplexer_30_out), .Q(Fila_32[16]), .preset(A));  // open: Qn, en, reset
  Multiplexer #(.select(2), .enable("false")) multiplexer_31 (
    .in0(Fila_32[16]), .in1(Fila_32[14]), .in2(1'b0), .out(multiplexer_31_out), .sel(DIR_t));  // open: in3
  D_Flip_Flop d_ff_29 (.clk(CLK), .D(multiplexer_31_out), .Q(Fila_32[15]), .preset(A));  // open: Qn, en, reset
  Multiplexer #(.select(2), .enable("false")) multiplexer_32 (
    .in0(Fila_32[15]), .in1(Fila_32[13]), .in2(1'b0), .out(multiplexer_32_out), .sel(DIR_t));  // open: in3
  D_Flip_Flop d_ff_30 (.clk(CLK), .D(multiplexer_32_out), .Q(Fila_32[14]), .preset(A));  // open: Qn, en, reset
  Multiplexer #(.select(2), .enable("false")) multiplexer_33 (
    .in0(Fila_32[14]), .in1(Fila_32[12]), .in2(1'b0), .out(multiplexer_33_out), .sel(DIR_t));  // open: in3
  D_Flip_Flop d_ff_31 (.clk(CLK), .D(multiplexer_33_out), .Q(Fila_32[13]), .preset(A));  // open: Qn, en, reset
  Multiplexer #(.select(2), .enable("false")) multiplexer_34 (
    .in0(Fila_32[13]), .in1(Fila_32[11]), .in2(1'b0), .out(multiplexer_34_out), .sel(DIR_t));  // open: in3
  D_Flip_Flop d_ff_32 (.clk(CLK), .D(multiplexer_34_out), .Q(Fila_32[12]));  // open: Qn, preset, en, reset

  // Other names for the same wires on the sheet: ACT = A; _3131_minus = Fila_32[0]; _3130_minus = Fila_32[1];
  //   _3129_minus = Fila_32[2]; _3128_minus = Fila_32[3]; _3127_minus = Fila_32[4]; _3126_minus = Fila_32[5];
  //   _3125_minus = Fila_32[6]; _3124_minus = Fila_32[7]; _3123_minus = Fila_32[8]; _3122_minus = Fila_32[9];
  //   _3121_minus = Fila_32[10]; _3120_minus = Fila_32[11]; _3119_minus = Fila_32[12]; _3118_minus = Fila_32[13];
  //   _3117_minus = Fila_32[14]; _3116_minus = Fila_32[15]; _3115_minus = Fila_32[16]; _3114_minus = Fila_32[17];
  //   _3113_minus = Fila_32[18]; _3112_minus = Fila_32[19]; _3111_minus = Fila_32[20]; _3110_minus = Fila_32[21];
  //   _319_minus = Fila_32[22]; _318_minus = Fila_32[23]; _317_minus = Fila_32[24]; _316_minus = Fila_32[25];
  //   _315_minus = Fila_32[26]; _314_minus = Fila_32[27]; _313_minus = Fila_32[28]; _312_minus = Fila_32[29];
  //   _311_minus = Fila_32[30]; _310_minus = Fila_32[31]
endmodule

module Mov (
  input  [31:0] Barra,
  input  Reiniciar,
  input  iniciar,
  input  Pausar,
  output [4:0] BolaPosCol,
  output [31:0] DataBolaCol
);

  wire and_7_out, and_10_out, and_17_out, and_18_out, and_35_out, CL, clock_1_out, CNT,
       controlled_buffer_1_out, d_ff_2_q, d_ff_3_q, d_ff_3_qn, GP, multiplexer_2_out, not_1_out, or_1_out,
       r0, r1, r2, r3, r4, r5, r6, r7, r8, r9, r10, r11, r12, r13, r14, r15, r16, r17, r18, r19, r20, r21,
       r22, r23, r24, r25, r26, r27, r28, r29, r30, r31;
  wire [4:0] BPosF, multiplexer_3_out, random_1_out;

  and and_1 (r0, DataBolaCol[31], Barra[31]);
  not not_1 (not_1_out, Reiniciar);
  Clock clock_1 (.out(clock_1_out));
  and and_2 (r2, DataBolaCol[29], Barra[29]);
  and and_3 (r1, DataBolaCol[30], Barra[30]);
  D_Flip_Flop d_ff_1 (.clk(CL), .Q(CNT), .preset(Reiniciar), .reset(controlled_buffer_1_out));  // open: D, Qn, en
  assign controlled_buffer_1_out = not_1_out ? GP : 1'bz;  // Controlled_Buffer controlled_buffer_1
  Multiplexer #(.enable("false")) multiplexer_1 (.in0(clock_1_out), .in1(1'b0), .out(CL), .sel(Pausar));
  and and_4 (r3, DataBolaCol[28], Barra[28]);
  and and_5 (r4, DataBolaCol[27], Barra[27]);
  and and_6 (r5, DataBolaCol[26], Barra[26]);
  and and_7 (and_7_out, ~BolaPosCol[0], ~BolaPosCol[1], ~BolaPosCol[2], ~BolaPosCol[3], ~BolaPosCol[4]);  // AND_Gate
  and and_8 (r6, DataBolaCol[25], Barra[25]);
  and and_9 (r7, DataBolaCol[24], Barra[24]);
  Decoder #(.select(5), .enable("false")) decoder_1 (
    .out0(DataBolaCol[0]), .out1(DataBolaCol[1]), .out2(DataBolaCol[2]), .out3(DataBolaCol[3]),
    .out4(DataBolaCol[4]), .out5(DataBolaCol[5]), .out6(DataBolaCol[6]), .out7(DataBolaCol[7]),
    .out8(DataBolaCol[8]), .out9(DataBolaCol[9]), .out10(DataBolaCol[10]), .out11(DataBolaCol[11]),
    .out12(DataBolaCol[12]), .out13(DataBolaCol[13]), .out14(DataBolaCol[14]), .out15(DataBolaCol[15]),
    .out16(DataBolaCol[16]), .out17(DataBolaCol[17]), .out18(DataBolaCol[18]), .out19(DataBolaCol[19]),
    .out20(DataBolaCol[20]), .out21(DataBolaCol[21]), .out22(DataBolaCol[22]), .out23(DataBolaCol[23]),
    .out24(DataBolaCol[24]), .out25(DataBolaCol[25]), .out26(DataBolaCol[26]), .out27(DataBolaCol[27]),
    .out28(DataBolaCol[28]), .out29(DataBolaCol[29]), .out30(DataBolaCol[30]), .out31(DataBolaCol[31]),
    .sel(BPosF));
  and and_10 (and_10_out, BolaPosCol[0], BolaPosCol[1], BolaPosCol[2], BolaPosCol[3], BolaPosCol[4]);
  D_Flip_Flop d_ff_2 (.Q(d_ff_2_q), .preset(and_10_out), .reset(and_7_out));  // open: clk, D, Qn, en
  and and_11 (r8, DataBolaCol[23], Barra[23]);
  and and_12 (r9, DataBolaCol[22], Barra[22]);
  and and_13 (r10, DataBolaCol[21], Barra[21]);
  Counter #(.width(5), .max('h1f)) counter_1 (
    .load(d_ff_2_q), .D(BolaPosCol), .count(CNT), .Q(BolaPosCol), .clk(CL));  // open: carry, clr
  and and_14 (r11, DataBolaCol[20], Barra[20]);
  and and_15 (r12, DataBolaCol[19], Barra[19]);
  and and_16 (r13, DataBolaCol[18], Barra[18]);
  and and_17 (and_17_out, ~BPosF[0], ~BPosF[1], ~BPosF[2], ~BPosF[3], ~BPosF[4]);  // AND_Gate
  and and_18 (and_18_out, BPosF[0], BPosF[1], BPosF[2], BPosF[3], BPosF[4]);
  and and_19 (r15, DataBolaCol[16], Barra[16]);
  and and_20 (r14, DataBolaCol[17], Barra[17]);
  D_Flip_Flop d_ff_3 (.Q(d_ff_3_q), .Qn(d_ff_3_qn), .preset(and_18_out), .reset(and_17_out));  // open: clk, D, en
  Random #(.width(5)) random_1 (.clk(iniciar), .out(random_1_out));  // open: next, clr
  and and_21 (r16, DataBolaCol[15], Barra[15]);
  Multiplexer #(.enable("false")) multiplexer_2 (.in0(d_ff_3_q), .in1(iniciar), .out(multiplexer_2_out), .sel(iniciar));
  and and_22 (r18, DataBolaCol[13], Barra[13]);
  and and_23 (r17, DataBolaCol[14], Barra[14]);
  Multiplexer #(.width(5), .enable("false")) multiplexer_3 (
    .in0(BPosF), .in1(random_1_out), .out(multiplexer_3_out), .sel(iniciar));
  and and_24 (r20, DataBolaCol[11], Barra[11]);
  and and_25 (r19, DataBolaCol[12], Barra[12]);
  and and_26 (r21, DataBolaCol[10], Barra[10]);
  Counter #(.width(5), .max('h1f)) counter_2 (
    .load(multiplexer_2_out), .D(multiplexer_3_out), .count(CNT), .Q(BPosF), .clk(CL));  // open: carry, clr
  and and_27 (r22, DataBolaCol[9], Barra[9]);
  and and_28 (r23, DataBolaCol[8], Barra[8]);
  and and_29 (r24, DataBolaCol[7], Barra[7]);
  and and_30 (r25, DataBolaCol[6], Barra[6]);
  and and_31 (r26, DataBolaCol[5], Barra[5]);
  and and_32 (r27, DataBolaCol[4], Barra[4]);
  and and_33 (r28, DataBolaCol[3], Barra[3]);
  and and_34 (r29, DataBolaCol[2], Barra[2]);
  and and_35 (and_35_out, ~BolaPosCol[0], ~BolaPosCol[1], ~BolaPosCol[2], ~BolaPosCol[3], ~BolaPosCol[4]);  // AND_Gate
  or or_1 (or_1_out, r31, r30, r29, r28, r27, r26, r25, r24, r23, r22, r21, r20, r19, r18, r17, r16, r15, r14, r13, r12, r11, r10, r9, r8, r7, r6, r5, r4, r3, r2, r1, r0);
  and and_36 (r31, DataBolaCol[0], Barra[0]);
  and and_37 (r30, DataBolaCol[1], Barra[1]);
  and and_38 (GP, and_35_out, ~or_1_out);  // AND_Gate

  // Other names for the same wires on the sheet: BPosC[4:0] = BolaPosCol; brr[31:0] = Barra; x31 = Barra[0];
  //   x30 = Barra[1]; x29 = Barra[2]; x28 = Barra[3]; x27 = Barra[4]; x26 = Barra[5]; x25 = Barra[6]; x24 = Barra[7];
  //   x23 = Barra[8]; x22 = Barra[9]; x21 = Barra[10]; x20 = Barra[11]; x19 = Barra[12]; x18 = Barra[13];
  //   x17 = Barra[14]; x16 = Barra[15]; x15 = Barra[16]; x14 = Barra[17]; x13 = Barra[18]; x12 = Barra[19];
  //   x11 = Barra[20]; x10 = Barra[21]; x9 = Barra[22]; x8 = Barra[23]; x7 = Barra[24]; x6 = Barra[25];
  //   x5 = Barra[26]; x4 = Barra[27]; x3 = Barra[28]; x2 = Barra[29]; x1 = Barra[30]; x0 = Barra[31];
  //   b31 = DataBolaCol[0]; b30 = DataBolaCol[1]; b29 = DataBolaCol[2]; b28 = DataBolaCol[3]; b27 = DataBolaCol[4];
  //   b26 = DataBolaCol[5]; b25 = DataBolaCol[6]; b24 = DataBolaCol[7]; b23 = DataBolaCol[8]; b22 = DataBolaCol[9];
  //   b21 = DataBolaCol[10]; b20 = DataBolaCol[11]; b19 = DataBolaCol[12]; b18 = DataBolaCol[13];
  //   b17 = DataBolaCol[14]; b16 = DataBolaCol[15]; b15 = DataBolaCol[16]; b14 = DataBolaCol[17];
  //   b13 = DataBolaCol[18]; b12 = DataBolaCol[19]; b11 = DataBolaCol[20]; b10 = DataBolaCol[21];
  //   b9 = DataBolaCol[22]; b8 = DataBolaCol[23]; b7 = DataBolaCol[24]; b6 = DataBolaCol[25]; b5 = DataBolaCol[26];
  //   b4 = DataBolaCol[27]; b3 = DataBolaCol[28]; b2 = DataBolaCol[29]; b1 = DataBolaCol[30]; b0 = DataBolaCol[31]

  // Notes on the sheet:
  //   Barra vs Bola
  //   Bola posición
  //   Posición al azar
endmodule
